// Logisim project Projeto_ULA FINAL.circ as structural Verilog: 22 circuits, main circuit main
module main (
  input  [15:0] A,
  input  [15:0] B,
  input  [2:0] \OPERAÇÃO ,
  output [15:0] SAIDA,
  output OVERFLOW
);

  ULA ula_1 (.Overflow(OVERFLOW), .SAIDA(SAIDA), .A(A), .B(B), .\Operação (\OPERAÇÃO ));
endmodule

module ULA (
  input  [15:0] B,
  input  [15:0] A,
  input  [2:0] \Operação ,
  output Overflow,
  output [15:0] SAIDA
);

  wire [15:0] \celula_aritmética_1_s0 , comparador_16bits_1_s, \lógicas_16_bits_1_s0 ;

  \Lógicas_16_bits  \lógicas_16_bits_1  (
    .A15(A[15]), .A14(A[14]), .A13(A[13]), .A12(A[12]), .A11(A[11]), .A10(A[10]), .A9(A[9]), .A8(A[8]),
    .A7(A[7]), .A6(A[6]), .A5(A[5]), .A4(A[4]), .A3(A[3]), .A2(A[2]), .A1(A[1]), .A0(A[0]), .B15(B[15]),
    .B14(B[14]), .B13(B[13]), .B12(B[12]), .B11(B[11]), .B10(B[10]), .B9(B[9]), .B8(B[8]), .B7(B[7]),
    .B6(B[6]), .B5(B[5]), .B4(B[4]), .B3(B[3]), .B2(B[2]), .B1(B[1]), .B0(B[0]), .\Operação (\Operação ),
    .S15(\lógicas_16_bits_1_s0 [15]), .S14(\lógicas_16_bits_1_s0 [14]), .S13(\lógicas_16_bits_1_s0 [13]),
    .S12(\lógicas_16_bits_1_s0 [12]), .S11(\lógicas_16_bits_1_s0 [11]), .S10(\lógicas_16_bits_1_s0 [10]),
    .S9(\lógicas_16_bits_1_s0 [9]), .S8(\lógicas_16_bits_1_s0 [8]), .S7(\lógicas_16_bits_1_s0 [7]),
    .S6(\lógicas_16_bits_1_s0 [6]), .S5(\lógicas_16_bits_1_s0 [5]), .S4(\lógicas_16_bits_1_s0 [4]),
    .S3(\lógicas_16_bits_1_s0 [3]), .S2(\lógicas_16_bits_1_s0 [2]), .S1(\lógicas_16_bits_1_s0 [1]),
    .S0(\lógicas_16_bits_1_s0 [0]));
  \Celula_Aritmética  \celula_aritmética_1  (
    .A0(A[0]), .A1(A[1]), .A2(A[2]), .A3(A[3]), .A4(A[4]), .A5(A[5]), .A6(A[6]), .A7(A[7]), .A8(A[8]),
    .A9(A[9]), .A10(A[10]), .A11(A[11]), .A12(A[12]), .A13(A[13]), .A14(A[14]), .A15(A[15]), .B0(B[0]),
    .B8(B[8]), .B1(B[1]), .B9(B[9]), .B2(B[2]), .B10(B[10]), .B3(B[3]), .B11(B[11]), .B4(B[4]), .B12(B[12]),
    .B5(B[5]), .B13(B[13]), .B6(B[6]), .B14(B[14]), .B7(B[7]), .B15(B[15]), .OPER(\Operação ),
    .S0(\celula_aritmética_1_s0 [0]), .S1(\celula_aritmética_1_s0 [1]), .S2(\celula_aritmética_1_s0 [2]),
    .S3(\celula_aritmética_1_s0 [3]), .S4(\celula_aritmética_1_s0 [4]), .S5(\celula_aritmética_1_s0 [5]),
    .S6(\celula_aritmética_1_s0 [6]), .S7(\celula_aritmética_1_s0 [7]), .S8(\celula_aritmética_1_s0 [8]),
    .S9(\celula_aritmética_1_s0 [9]), .S10(\celula_aritmética_1_s0 [10]), .S11(\celula_aritmética_1_s0 [11]),
    .S12(\celula_aritmética_1_s0 [12]), .S13(\celula_aritmética_1_s0 [13]),
    .S14(\celula_aritmética_1_s0 [14]), .S15(\celula_aritmética_1_s0 [15]), .Overflow(Overflow));
  MUX_8_1_16Bits mux_8_1_16bits_1 (
    .D0(\lógicas_16_bits_1_s0 ), .D1(\lógicas_16_bits_1_s0 ), .D2(\lógicas_16_bits_1_s0 ),
    .D3(comparador_16bits_1_s), .D4(comparador_16bits_1_s), .D5(comparador_16bits_1_s),
    .D6(\celula_aritmética_1_s0 ), .D7(\celula_aritmética_1_s0 ), .in_8(\Operação ), .S(SAIDA));
  Comparador_16Bits comparador_16bits_1 (
    .A15(A[15]), .A14(A[14]), .A13(A[13]), .A12(A[12]), .A11(A[11]), .A10(A[10]), .A9(A[9]), .A8(A[8]),
    .A7(A[7]), .A6(A[6]), .A5(A[5]), .A4(A[4]), .A3(A[3]), .A2(A[2]), .A1(A[1]), .A0(A[0]), .B15(B[15]),
    .B14(B[14]), .B13(B[13]), .B12(B[12]), .B11(B[11]), .B10(B[10]), .B9(B[9]), .B8(B[8]), .B7(B[7]),
    .B6(B[6]), .B5(B[5]), .B4(B[4]), .B3(B[3]), .B2(B[2]), .B1(B[1]), .B0(B[0]), .OPER(\Operação ),
    .S(comparador_16bits_1_s));
endmodule

module \Lógicas_1_bit  (
  input  A0,
  input  B0,
  input  [2:0] \Operação ,
  output S0
);

  wire and_1_out, not_1_out, or_1_out;

  not not_1 (not_1_out, A0);
  and and_1 (and_1_out, A0, B0);
  or or_1 (or_1_out, A0, B0);
  MUX_8para1 mux_8para1_1 (
    .D7(1'b0), .D6(1'b0), .D5(1'b0), .D4(1'b0), .D3(1'b0), .D2(or_1_out), .D1(and_1_out), .D0(not_1_out),
    .S0(\Operação [0]), .S1(\Operação [1]), .S2(\Operação [2]), .F(S0));
endmodule

module \Lógicas_2_bits  (
  input  A1,
  input  A0,
  input  B1,
  input  B0,
  input  [2:0] \Operação ,
  output S1,
  output S0
);

  \Lógicas_1_bit  \lógicas_1_bit_1  (.A0(A0), .B0(B0), .\Operação (\Operação ), .S0(S0));
  \Lógicas_1_bit  \lógicas_1_bit_2  (.A0(A1), .B0(B1), .\Operação (\Operação ), .S0(S1));
endmodule

module \Lógicas_4_bits  (
  input  A3,
  input  A2,
  input  A1,
  input  A0,
  input  B3,
  input  B2,
  input  B1,
  input  B0,
  input  [2:0] \Operação ,
  output S3,
  output S2,
  output S1,
  output S0
);

  \Lógicas_2_bits  \lógicas_2_bits_1  (.A1(A1), .A0(A0), .B1(B1), .B0(B0), .\Operação (\Operação ), .S1(S1), .S0(S0));
  \Lógicas_2_bits  \lógicas_2_bits_2  (.A1(A3), .A0(A2), .B1(B3), .B0(B2), .\Operação (\Operação ), .S1(S3), .S0(S2));
endmodule

module \Lógicas_8_bits  (
  input  A7,
  input  A6,
  input  A5,
  input  A4,
  input  A3,
  input  A2,
  input  A1,
  input  A0,
  input  B7,
  input  B6,
  input  B5,
  input  B4,
  input  B3,
  input  B2,
  input  B1,
  input  B0,
  input  [2:0] \Operação ,
  output S7,
  output S6,
  output S5,
  output S4,
  output S3,
  output S2,
  output S1,
  output S0
);

  \Lógicas_4_bits  \lógicas_4_bits_1  (
    .A3(A3), .A2(A2), .A1(A1), .A0(A0), .B3(B3), .B2(B2), .B1(B1), .B0(B0), .\Operação (\Operação ), .S3(S3),
    .S2(S2), .S1(S1), .S0(S0));
  \Lógicas_4_bits  \lógicas_4_bits_2  (
    .A3(A7), .A2(A6), .A1(A5), .A0(A4), .B3(B7), .B2(B6), .B1(B5), .B0(B4), .\Operação (\Operação ), .S3(S7),
    .S2(S6), .S1(S5), .S0(S4));
endmodule

// CELULA LÓGICA
module \Lógicas_16_bits  (
  input  A15,
  input  A14,
  input  A13,
  input  A12,
  input  A11,
  input  A10,
  input  A9,
  input  A8,
  input  A7,
  input  A6,
  input  A5,
  input  A4,
  input  A3,
  input  A2,
  input  A1,
  input  A0,
  input  B15,
  input  B14,
  input  B13,
  input  B12,
  input  B11,
  input  B10,
  input  B9,
  input  B8,
  input  B7,
  input  B6,
  input  B5,
  input  B4,
  input  B3,
  input  B2,
  input  B1,
  input  B0,
  input  [2:0] \Operação ,
  output S15,
  output S14,
  output S13,
  output S12,
  output S11,
  output S10,
  output S9,
  output S8,
  output S7,
  output S6,
  output S5,
  output S4,
  output S3,
  output S2,
  output S1,
  output S0
);

  \Lógicas_8_bits  \lógicas_8_bits_1  (
    .A7(A7), .A6(A6), .A5(A5), .A4(A4), .A3(A3), .A2(A2), .A1(A1), .A0(A0), .B7(B7), .B6(B6), .B5(B5),
    .B4(B4), .B3(B3), .B2(B2), .B1(B1), .B0(B0), .\Operação (\Operação ), .S7(S7), .S6(S6), .S5(S5), .S4(S4),
    .S3(S3), .S2(S2), .S1(S1), .S0(S0));
  \Lógicas_8_bits  \lógicas_8_bits_2  (
    .A7(A15), .A6(A14), .A5(A13), .A4(A12), .A3(A11), .A2(A10), .A1(A9), .A0(A8), .B7(B15), .B6(B14),
    .B5(B13), .B4(B12), .B3(B11), .B2(B10), .B1(B9), .B0(B8), .\Operação (\Operação ), .S7(S15), .S6(S14),
    .S5(S13), .S4(S12), .S3(S11), .S2(S10), .S1(S9), .S0(S8));
endmodule

module Comparador_1Bit (
  input  A,
  input  B,
  input  AMaior,
  input  BMaior,
  input  ABIguais,
  output AMaior_2,
  output BMaior_2,
  output ABIguais_2
);

  wire and_1_out, and_2_out, and_3_out, and_4_out, and_5_out, not_1_out, not_2_out, not_3_out, not_4_out,
       not_5_out, not_6_out, not_7_out, not_8_out, not_9_out, not_10_out, not_11_out, not_12_out;

  not not_1 (not_1_out, B);
  not not_2 (not_2_out, BMaior);
  not not_3 (not_3_out, AMaior);
  not not_4 (not_4_out, ABIguais);
  not not_5 (not_5_out, A);
  not not_6 (not_6_out, AMaior);
  not not_7 (not_7_out, A);
  not not_8 (not_8_out, B);
  not not_9 (not_9_out, AMaior);
  not not_10 (not_10_out, BMaior);
  not not_11 (not_11_out, BMaior);
  not not_12 (not_12_out, AMaior);
  and and_1 (and_1_out, A, not_1_out, not_2_out);
  and and_2 (and_2_out, not_3_out, not_4_out);
  and and_3 (and_3_out, not_5_out, B, not_6_out);
  and and_4 (and_4_out, not_7_out, not_8_out, not_9_out, not_10_out);
  and and_5 (and_5_out, A, B, not_12_out, not_11_out);
  or or_1 (AMaior_2, AMaior, and_1_out);
  or or_2 (BMaior_2, and_2_out, and_3_out);
  or or_3 (ABIguais_2, and_4_out, and_5_out);
endmodule

module Somador_1_bit (
  input  Carry_In,
  input  A,
  input  B,
  output S,
  output Carry_Out
);

  wire and_1_out, and_2_out, xor_1_out;

  and and_1 (and_1_out, B, A);
  xor xor_1 (xor_1_out, A, B);
  or or_1 (Carry_Out, and_1_out, and_2_out);
  and and_2 (and_2_out, xor_1_out, Carry_In);
  xor xor_2 (S, Carry_In, xor_1_out);
endmodule

module Somador_2_bits (
  input  Carry_In,
  input  A0,
  input  B0,
  input  A1,
  input  B1,
  output S0,
  output S1,
  output Carry_Out
);

  wire somador_1_bit_1_carry_out;

  Somador_1_bit somador_1_bit_1 (.A(A0), .B(B0), .Carry_In(Carry_In), .Carry_Out(somador_1_bit_1_carry_out), .S(S0));
  Somador_1_bit somador_1_bit_2 (.A(A1), .B(B1), .Carry_In(somador_1_bit_1_carry_out), .Carry_Out(Carry_Out), .S(S1));
endmodule

module Somador_4_bits (
  input  Carry_In,
  input  A0,
  input  B0,
  input  A1,
  input  B1,
  input  A2,
  input  B2,
  input  A3,
  input  B3,
  output S0,
  output S1,
  output S2,
  output S3,
  output Carry_Out
);

  wire somador_2_bits_1_carry_out;

  Somador_2_bits somador_2_bits_1 (
    .A0(A0), .B0(B0), .A1(A1), .B1(B1), .Carry_In(Carry_In), .Carry_Out(somador_2_bits_1_carry_out), .S0(S0),
    .S1(S1));
  Somador_2_bits somador_2_bits_2 (
    .A0(A2), .B0(B2), .A1(A3), .B1(B3), .Carry_In(somador_2_bits_1_carry_out), .Carry_Out(Carry_Out),
    .S0(S2), .S1(S3));
endmodule

module Somador_8_bits (
  input  Carry_In,
  input  A0,
  input  B0,
  input  A1,
  input  B1,
  input  A2,
  input  B2,
  input  A3,
  input  B3,
  input  A4,
  input  B4,
  input  A5,
  input  B5,
  input  A6,
  input  B6,
  input  A7,
  input  B7,
  output S0,
  output S1,
  output S2,
  output S3,
  output S4,
  output S5,
  output S6,
  output S7,
  output Carry_Out
);

  wire somador_4_bits_1_carry_out;

  Somador_4_bits somador_4_bits_1 (
    .A0(A0), .B0(B0), .A1(A1), .B1(B1), .A2(A2), .B2(B2), .A3(A3), .B3(B3), .Carry_In(Carry_In),
    .Carry_Out(somador_4_bits_1_carry_out), .S0(S0), .S1(S1), .S2(S2), .S3(S3));
  Somador_4_bits somador_4_bits_2 (
    .A0(A4), .B0(B4), .A1(A5), .B1(B5), .A2(A6), .B2(B6), .A3(A7), .B3(B7),
    .Carry_In(somador_4_bits_1_carry_out), .Carry_Out(Carry_Out), .S0(S4), .S1(S5), .S2(S6), .S3(S7));
endmodule

module Somador_16_bits (
  input  A0,
  input  B0,
  input  A1,
  input  Carry_In,
  input  B1,
  input  A2,
  input  B2,
  input  A3,
  input  B3,
  input  A4,
  input  B4,
  input  A5,
  input  B5,
  input  A6,
  input  B6,
  input  A7,
  input  B7,
  input  A8,
  input  B8,
  input  A9,
  input  B9,
  input  A10,
  input  B10,
  input  A11,
  input  B11,
  input  A12,
  input  B12,
  input  A13,
  input  B13,
  input  A14,
  input  B14,
  input  A15,
  input  B15,
  output S0,
  output S1,
  output S2,
  output S3,
  output S4,
  output S5,
  output S6,
  output S7,
  output S8,
  output S9,
  output S10,
  output S11,
  output S12,
  output S13,
  output S14,
  output S15,
  output Carry_Out
);

  wire somador_8_bits_1_carry_out;

  Somador_8_bits somador_8_bits_1 (
    .A0(A0), .B0(B0), .A1(A1), .B1(B1), .A2(A2), .B2(B2), .A3(A3), .B3(B3), .A4(A4), .B4(B4), .A5(A5),
    .B5(B5), .A6(A6), .B6(B6), .A7(A7), .B7(B7), .Carry_In(Carry_In), .Carry_Out(somador_8_bits_1_carry_out),
    .S0(S0), .S1(S1), .S2(S2), .S3(S3), .S4(S4), .S5(S5), .S6(S6), .S7(S7));
  Somador_8_bits somador_8_bits_2 (
    .A0(A8), .B0(B8), .A1(A9), .B1(B9), .A2(A10), .B2(B10), .A3(A11), .B3(B11), .A4(A12), .B4(B12), .A5(A13),
    .B5(B13), .A6(A14), .B6(B14), .A7(A15), .B7(B15), .Carry_In(somador_8_bits_1_carry_out),
    .Carry_Out(Carry_Out), .S0(S8), .S1(S9), .S2(S10), .S3(S11), .S4(S12), .S5(S13), .S6(S14), .S7(S15));
endmodule

// CELULA ARITMÉTICA
module \Celula_Aritmética  (
  input  A0,
  input  A1,
  input  A2,
  input  A3,
  input  A4,
  input  A5,
  input  A6,
  input  A7,
  input  A8,
  input  A9,
  input  A10,
  input  A11,
  input  A12,
  input  A13,
  input  A14,
  input  A15,
  input  B0,
  input  B8,
  input  B1,
  input  B9,
  input  B2,
  input  B10,
  input  B3,
  input  [2:0] OPER,
  input  B11,
  input  B4,
  input  B12,
  input  B5,
  input  B13,
  input  B6,
  input  B14,
  input  B7,
  input  B15,
  output S0,
  output S1,
  output S2,
  output S3,
  output S4,
  output S5,
  output S6,
  output S7,
  output S8,
  output S9,
  output S10,
  output S11,
  output S12,
  output S13,
  output S14,
  output S15,
  output Overflow
);

  wire and_1_out, and_2_out, not_1_out, not_2_out, not_3_out, xor_1_out, xor_2_out, xor_3_out, xor_4_out,
       xor_5_out, xor_6_out, xor_7_out, xor_8_out, xor_9_out, xor_10_out, xor_11_out, xor_12_out, xor_13_out,
       xor_14_out, xor_15_out, xor_16_out;

  xor xor_1 (xor_1_out, B0, OPER[0]);
  xor xor_2 (xor_2_out, B1, OPER[0]);
  xor xor_3 (xor_3_out, B2, OPER[0]);
  xor xor_4 (xor_4_out, B3, OPER[0]);
  xor xor_5 (xor_5_out, B4, OPER[0]);
  xor xor_6 (xor_6_out, B5, OPER[0]);
  xor xor_7 (xor_7_out, B6, OPER[0]);
  xor xor_8 (xor_8_out, B7, OPER[0]);
  xor xor_9 (xor_9_out, B8, OPER[0]);
  xor xor_10 (xor_10_out, B9, OPER[0]);
  xor xor_11 (xor_11_out, B10, OPER[0]);
  xor xor_12 (xor_12_out, B11, OPER[0]);
  xor xor_13 (xor_13_out, B12, OPER[0]);
  xor xor_14 (xor_14_out, B13, OPER[0]);
  xor xor_15 (xor_15_out, B14, OPER[0]);
  xor xor_16 (xor_16_out, B15, OPER[0]);
  Somador_16_bits somador_16_bits_1 (
    .A0(A0), .B0(xor_1_out), .A1(A1), .B1(xor_2_out), .A2(A2), .B2(xor_3_out), .A3(A3), .B3(xor_4_out),
    .A4(A4), .B4(xor_5_out), .A5(A5), .B5(xor_6_out), .A6(A6), .B6(xor_7_out), .A7(A7), .B7(xor_8_out),
    .A8(A8), .B8(xor_9_out), .A9(A9), .B9(xor_10_out), .A10(A10), .B10(xor_11_out), .A11(A11),
    .B11(xor_12_out), .A12(A12), .B12(xor_13_out), .A13(A13), .B13(xor_14_out), .A14(A14), .B14(xor_15_out),
    .A15(A15), .B15(xor_16_out), .Carry_In(OPER[0]), .S0(S0), .S1(S1), .S2(S2), .S3(S3), .S4(S4), .S5(S5),
    .S6(S6), .S7(S7), .S8(S8), .S9(S9), .S10(S10), .S11(S11), .S12(S12), .S13(S13), .S14(S14), .S15(S15));  // open: Carry_Out
  not not_1 (not_1_out, S15);
  not not_2 (not_2_out, A15);
  not not_3 (not_3_out, B15);
  and and_1 (and_1_out, A15, B15, not_1_out);
  and and_2 (and_2_out, not_2_out, not_3_out, S15);
  or or_1 (Overflow, and_1_out, and_2_out);
endmodule

// CELULA COMPARADORA
module Comparador_16Bits (
  input  A15,
  input  A14,
  input  A13,
  input  A12,
  input  A11,
  input  A10,
  input  A9,
  input  A8,
  input  A7,
  input  A6,
  input  A5,
  input  A4,
  input  A3,
  input  A2,
  input  A1,
  input  A0,
  input  B15,
  input  B14,
  input  B13,
  input  B12,
  input  B11,
  input  B10,
  input  B9,
  input  B8,
  input  B7,
  input  B6,
  input  B5,
  input  B4,
  input  B3,
  input  B2,
  input  B1,
  input  B0,
  input  [2:0] OPER,
  output [15:0] S
);

  wire comparador_1bit_1_abiguais_2, comparador_1bit_1_amaior_2, comparador_1bit_1_bmaior_2,
       comparador_1bit_2_abiguais_2, comparador_1bit_2_amaior_2, comparador_1bit_2_bmaior_2,
       comparador_1bit_3_abiguais_2, comparador_1bit_3_amaior_2, comparador_1bit_3_bmaior_2,
       comparador_1bit_4_abiguais_2, comparador_1bit_4_amaior_2, comparador_1bit_4_bmaior_2,
       comparador_1bit_5_abiguais_2, comparador_1bit_5_amaior_2, comparador_1bit_5_bmaior_2,
       comparador_1bit_6_abiguais_2, comparador_1bit_6_amaior_2, comparador_1bit_6_bmaior_2,
       comparador_1bit_7_abiguais_2, comparador_1bit_7_amaior_2, comparador_1bit_7_bmaior_2,
       comparador_1bit_8_abiguais_2, comparador_1bit_8_amaior_2, comparador_1bit_8_bmaior_2,
       comparador_1bit_9_abiguais_2, comparador_1bit_9_amaior_2, comparador_1bit_9_bmaior_2,
       comparador_1bit_10_abiguais_2, comparador_1bit_10_amaior_2, comparador_1bit_10_bmaior_2,
       comparador_1bit_11_abiguais_2, comparador_1bit_11_amaior_2, comparador_1bit_11_bmaior_2,
       comparador_1bit_12_abiguais_2, comparador_1bit_12_amaior_2, comparador_1bit_12_bmaior_2,
       comparador_1bit_13_abiguais_2, comparador_1bit_13_amaior_2, comparador_1bit_13_bmaior_2,
       comparador_1bit_14_abiguais_2, comparador_1bit_14_amaior_2, comparador_1bit_14_bmaior_2,
       comparador_1bit_15_abiguais_2, comparador_1bit_15_amaior_2, comparador_1bit_15_bmaior_2,
       comparador_1bit_16_abiguais_2, comparador_1bit_16_amaior_2, comparador_1bit_16_bmaior_2;
  wire [0:0] mux_8para1_1_f;

  Comparador_1Bit comparador_1bit_1 (
    .A(A15), .B(B15), .AMaior(1'b0), .BMaior(1'b0), .ABIguais(1'b1), .AMaior_2(comparador_1bit_1_amaior_2),
    .BMaior_2(comparador_1bit_1_bmaior_2), .ABIguais_2(comparador_1bit_1_abiguais_2));
  Comparador_1Bit comparador_1bit_2 (
    .A(A14), .B(B14), .AMaior(comparador_1bit_1_amaior_2), .BMaior(comparador_1bit_1_bmaior_2),
    .ABIguais(comparador_1bit_1_abiguais_2), .AMaior_2(comparador_1bit_2_amaior_2),
    .BMaior_2(comparador_1bit_2_bmaior_2), .ABIguais_2(comparador_1bit_2_abiguais_2));
  Comparador_1Bit comparador_1bit_3 (
    .A(A13), .B(B13), .AMaior(comparador_1bit_2_amaior_2), .BMaior(comparador_1bit_2_bmaior_2),
    .ABIguais(comparador_1bit_2_abiguais_2), .AMaior_2(comparador_1bit_3_amaior_2),
    .BMaior_2(comparador_1bit_3_bmaior_2), .ABIguais_2(comparador_1bit_3_abiguais_2));
  Comparador_1Bit comparador_1bit_4 (
    .A(A12), .B(B12), .AMaior(comparador_1bit_3_amaior_2), .BMaior(comparador_1bit_3_bmaior_2),
    .ABIguais(comparador_1bit_3_abiguais_2), .AMaior_2(comparador_1bit_4_amaior_2),
    .BMaior_2(comparador_1bit_4_bmaior_2), .ABIguais_2(comparador_1bit_4_abiguais_2));
  Comparador_1Bit comparador_1bit_5 (
    .A(A11), .B(B11), .AMaior(comparador_1bit_4_amaior_2), .BMaior(comparador_1bit_4_bmaior_2),
    .ABIguais(comparador_1bit_4_abiguais_2), .AMaior_2(comparador_1bit_5_amaior_2),
    .BMaior_2(comparador_1bit_5_bmaior_2), .ABIguais_2(comparador_1bit_5_abiguais_2));
  Comparador_1Bit comparador_1bit_6 (
    .A(A10), .B(B10), .AMaior(comparador_1bit_5_amaior_2), .BMaior(comparador_1bit_5_bmaior_2),
    .ABIguais(comparador_1bit_5_abiguais_2), .AMaior_2(comparador_1bit_6_amaior_2),
    .BMaior_2(comparador_1bit_6_bmaior_2), .ABIguais_2(comparador_1bit_6_abiguais_2));
  Comparador_1Bit comparador_1bit_7 (
    .A(A9), .B(B9), .AMaior(comparador_1bit_6_amaior_2), .BMaior(comparador_1bit_6_bmaior_2),
    .ABIguais(comparador_1bit_6_abiguais_2), .AMaior_2(comparador_1bit_7_amaior_2),
    .BMaior_2(comparador_1bit_7_bmaior_2), .ABIguais_2(comparador_1bit_7_abiguais_2));
  Comparador_1Bit comparador_1bit_8 (
    .A(A8), .B(B8), .AMaior(comparador_1bit_7_amaior_2), .BMaior(comparador_1bit_7_bmaior_2),
    .ABIguais(comparador_1bit_7_abiguais_2), .AMaior_2(comparador_1bit_8_amaior_2),
    .BMaior_2(comparador_1bit_8_bmaior_2), .ABIguais_2(comparador_1bit_8_abiguais_2));
  Comparador_1Bit comparador_1bit_9 (
    .A(A7), .B(B7), .AMaior(comparador_1bit_8_amaior_2), .BMaior(comparador_1bit_8_bmaior_2),
    .ABIguais(comparador_1bit_8_abiguais_2), .AMaior_2(comparador_1bit_9_amaior_2),
    .BMaior_2(comparador_1bit_9_bmaior_2), .ABIguais_2(comparador_1bit_9_abiguais_2));
  MUX_8para1 mux_8para1_1 (
    .D7(1'b0), .D6(1'b0), .D5(comparador_1bit_16_bmaior_2), .D4(comparador_1bit_16_amaior_2),
    .D3(comparador_1bit_16_abiguais_2), .D2(1'b0), .D1(1'b0), .D0(1'b0), .S0(OPER[0]), .S1(OPER[1]),
    .S2(OPER[2]), .F(mux_8para1_1_f[0]));
  Comparador_1Bit comparador_1bit_10 (
    .A(A6), .B(B6), .AMaior(comparador_1bit_9_amaior_2), .BMaior(comparador_1bit_9_bmaior_2),
    .ABIguais(comparador_1bit_9_abiguais_2), .AMaior_2(comparador_1bit_10_amaior_2),
    .BMaior_2(comparador_1bit_10_bmaior_2), .ABIguais_2(comparador_1bit_10_abiguais_2));
  Comparador_1Bit comparador_1bit_11 (
    .A(A5), .B(B5), .AMaior(comparador_1bit_10_amaior_2), .BMaior(comparador_1bit_10_bmaior_2),
    .ABIguais(comparador_1bit_10_abiguais_2), .AMaior_2(comparador_1bit_11_amaior_2),
    .BMaior_2(comparador_1bit_11_bmaior_2), .ABIguais_2(comparador_1bit_11_abiguais_2));
  MUX_8_1_16Bits mux_8_1_16bits_1 (
    .D0({16{1'b0}}), .D1({16{1'b1}}), .in_8({2'b00, mux_8para1_1_f[0]}), .S(S));  // open: D2, D3, D4, D5, D6, D7
  Comparador_1Bit comparador_1bit_12 (
    .A(A4), .B(B4), .AMaior(comparador_1bit_11_amaior_2), .BMaior(comparador_1bit_11_bmaior_2),
    .ABIguais(comparador_1bit_11_abiguais_2), .AMaior_2(comparador_1bit_12_amaior_2),
    .BMaior_2(comparador_1bit_12_bmaior_2), .ABIguais_2(comparador_1bit_12_abiguais_2));
  Comparador_1Bit comparador_1bit_13 (
    .A(A3), .B(B3), .AMaior(comparador_1bit_12_amaior_2), .BMaior(comparador_1bit_12_bmaior_2),
    .ABIguais(comparador_1bit_12_abiguais_2), .AMaior_2(comparador_1bit_13_amaior_2),
    .BMaior_2(comparador_1bit_13_bmaior_2), .ABIguais_2(comparador_1bit_13_abiguais_2));
  Comparador_1Bit comparador_1bit_14 (
    .A(A2), .B(B2), .AMaior(comparador_1bit_13_amaior_2), .BMaior(comparador_1bit_13_bmaior_2),
    .ABIguais(comparador_1bit_13_abiguais_2), .AMaior_2(comparador_1bit_14_amaior_2),
    .BMaior_2(comparador_1bit_14_bmaior_2), .ABIguais_2(comparador_1bit_14_abiguais_2));
  Comparador_1Bit comparador_1bit_15 (
    .A(A1), .B(B1), .AMaior(comparador_1bit_14_amaior_2), .BMaior(comparador_1bit_14_bmaior_2),
    .ABIguais(comparador_1bit_14_abiguais_2), .AMaior_2(comparador_1bit_15_amaior_2),
    .BMaior_2(comparador_1bit_15_bmaior_2), .ABIguais_2(comparador_1bit_15_abiguais_2));
  Comparador_1Bit comparador_1bit_16 (
    .A(A0), .B(B0), .AMaior(comparador_1bit_15_amaior_2), .BMaior(comparador_1bit_15_bmaior_2),
    .ABIguais(comparador_1bit_15_abiguais_2), .AMaior_2(comparador_1bit_16_amaior_2),
    .BMaior_2(comparador_1bit_16_bmaior_2), .ABIguais_2(comparador_1bit_16_abiguais_2));
endmodule

// MUX-8/1
module MUX_2para1 (
  input  D0,
  input  D1,
  input  S0,
  output F
);

  wire and_1_out, and_2_out, not_1_out;

  and and_1 (and_1_out, D0, not_1_out);
  not not_1 (not_1_out, S0);
  and and_2 (and_2_out, D1, S0);
  or or_1 (F, and_1_out, and_2_out);
endmodule

module MUX_4para1 (
  input  S1,
  input  S0,
  input  D0,
  input  D1,
  input  D2,
  input  D3,
  output F
);

  wire and_1_out, and_2_out, and_3_out, and_4_out, not_1_out, not_2_out;

  not not_1 (not_1_out, S1);
  not not_2 (not_2_out, S0);
  and and_1 (and_1_out, not_1_out, not_2_out, D0);
  and and_2 (and_2_out, not_1_out, S0, D1);
  and and_3 (and_3_out, S1, not_2_out, D2);
  and and_4 (and_4_out, S1, S0, D3);
  or or_1 (F, and_1_out, and_2_out, and_3_out, and_4_out);
endmodule

// MUX-8/1
module MUX_8para1 (
  input  S0,
  input  S1,
  input  S2,
  input  D7,
  input  D6,
  input  D5,
  input  D4,
  input  D3,
  input  D2,
  input  D1,
  input  D0,
  output F
);

  wire mux_4para1_1_f, mux_4para1_2_f;

  MUX_4para1 mux_4para1_1 (.D0(D0), .D1(D1), .D2(D2), .D3(D3), .S1(S1), .S0(S0), .F(mux_4para1_1_f));
  MUX_4para1 mux_4para1_2 (.D0(D4), .D1(D5), .D2(D6), .D3(D7), .S1(S1), .S0(S0), .F(mux_4para1_2_f));
  MUX_2para1 mux_2para1_1 (.D0(mux_4para1_1_f), .D1(mux_4para1_2_f), .S0(S2), .F(F));
endmodule

module MUX_8_1_2Bits (
  input  [1:0] D0,
  input  [1:0] D1,
  input  [2:0] OPER,
  input  [1:0] D2,
  input  [1:0] D3,
  input  [1:0] D4,
  input  [1:0] D5,
  input  [1:0] D6,
  input  [1:0] D7,
  output [1:0] S
);

  MUX_8para1 mux_8para1_1 (
    .D7(D7[0]), .D6(D6[0]), .D5(D5[0]), .D4(D4[0]), .D3(D3[0]), .D2(D2[0]), .D1(D1[0]), .D0(D0[0]),
    .S0(OPER[0]), .S1(OPER[1]), .S2(OPER[2]), .F(S[0]));
  MUX_8para1 mux_8para1_2 (
    .D7(D7[1]), .D6(D6[1]), .D5(D5[1]), .D4(D4[1]), .D3(D3[1]), .D2(D2[1]), .D1(D1[1]), .D0(D0[1]),
    .S0(OPER[0]), .S1(OPER[1]), .S2(OPER[2]), .F(S[1]));
endmodule

module MUX_8_1_4Bits (
  input  [3:0] D0,
  input  [3:0] D1,
  input  [3:0] D2,
  input  [3:0] D3,
  input  [3:0] D4,
  input  [3:0] D5,
  input  [3:0] D6,
  input  [2:0] OPER,
  input  [3:0] D7,
  output [3:0] out_10
);

  MUX_8_1_2Bits mux_8_1_2bits_1 (
    .D0(D0[1:0]), .D1(D1[1:0]), .D2(D2[1:0]), .D3(D3[1:0]), .D4(D4[1:0]), .D5(D5[1:0]), .D6(D6[1:0]),
    .D7(D7[1:0]), .OPER(OPER), .S(out_10[1:0]));
  MUX_8_1_2Bits mux_8_1_2bits_2 (
    .D0(D0[3:2]), .D1(D1[3:2]), .D2(D2[3:2]), .D3(D3[3:2]), .D4(D4[3:2]), .D5(D5[3:2]), .D6(D6[3:2]),
    .D7(D7[3:2]), .OPER(OPER), .S(out_10[3:2]));
endmodule

module MUX_8_1_8Bits (
  input  [7:0] D0,
  input  [7:0] D1,
  input  [7:0] D2,
  input  [7:0] D3,
  input  [7:0] D4,
  input  [7:0] D5,
  input  [7:0] D6,
  input  [7:0] D7,
  input  [2:0] OPER,
  output [7:0] S
);

  MUX_8_1_4Bits mux_8_1_4bits_1 (
    .D0(D0[3:0]), .D1(D1[3:0]), .D2(D2[3:0]), .D3(D3[3:0]), .D4(D4[3:0]), .D5(D5[3:0]), .D6(D6[3:0]),
    .D7(D7[3:0]), .OPER(OPER), .out_10(S[3:0]));
  MUX_8_1_4Bits mux_8_1_4bits_2 (
    .D0(D0[7:4]), .D1(D1[7:4]), .D2(D2[7:4]), .D3(D3[7:4]), .D4(D4[7:4]), .D5(D5[7:4]), .D6(D6[7:4]),
    .D7(D7[7:4]), .OPER(OPER), .out_10(S[7:4]));
endmodule

// MUX-8/1
module MUX_8_1_16Bits (
  input  [15:0] D0,
  input  [15:0] D1,
  input  [15:0] D2,
  input  [15:0] D3,
  input  [15:0] D4,
  input  [15:0] D5,
  input  [15:0] D6,
  input  [2:0] in_8,
  input  [15:0] D7,
  output [15:0] S
);

  MUX_8_1_8Bits mux_8_1_8bits_1 (
    .D0(D0[7:0]), .D1(D1[7:0]), .D2(D2[7:0]), .D3(D3[7:0]), .D4(D4[7:0]), .D5(D5[7:0]), .D6(D6[7:0]),
    .D7(D7[7:0]), .OPER(in_8), .S(S[7:0]));
  MUX_8_1_8Bits mux_8_1_8bits_2 (
    .D0(D0[15:8]), .D1(D1[15:8]), .D2(D2[15:8]), .D3(D3[15:8]), .D4(D4[15:8]), .D5(D5[15:8]), .D6(D6[15:8]),
    .D7(D7[15:8]), .OPER(in_8), .S(S[15:8]));
endmodule
